# Fritzing sketch full_circuit (saved by Fritzing 0.9.1b)
breadboards: 1

parts:
  Button = Pushbutton [package=THT]
  Part1 = Arduino Uno (Rev3)
  Speaker = Piezo Speaker
  Box_Servo = Basic Servo
  Bird_Servo = Basic Servo
  Background_Servo = Basic Servo
  Magnet_Sensor = Reed switch [package=THT]

nets:
  GND: Button.leg0, Part1.GND, Speaker.pin1, Box_Servo.gnd, Bird_Servo.gnd, Background_Servo.gnd, Magnet_Sensor.pin_1
  N1: Button.leg1, Part1.D10_PWM/SS
  N2: Part1.D8, Bird_Servo.pulse
  N3: Part1.D9_PWM, Box_Servo.pulse
  N4: Part1.D5_PWM, Speaker.pin2
  N5: Part1.D6_PWM, Magnet_Sensor.pin_2
  N6: Part1.D7, Background_Servo.pulse
  VCC: Part1.5V, Box_Servo.vcc, Bird_Servo.vcc, Background_Servo.vcc
